# Fritzing sketch Attendance_facerecog_with_temp_Fritzing (saved by Fritzing 0.9.3b)
breadboards: 1

parts:
  Raspberry_Pi1 = Raspberry Pi B+
  U1 = MLX90614 [package=to-39]
  IC1 = Rasberry Pi NIOR Camera [chip_label=IC package="DIP (Dual Inline) [THT]"]  # not connected
  LED1 = smd LED [color="Red (633nm)" package="1206 [SMD]"]

nets:
  N1: Raspberry_Pi1.GPIO2, U1.PWM_SDA
  N2: Raspberry_Pi1.GPIO3, U1.SCL_VZ
  GND: Raspberry_Pi1.GND, U1.VSS, LED1.cathode
  5V: Raspberry_Pi1.5V, U1.VDD, LED1.anode

notes:
  Non Contact Temperature
  Sensor - i2c Communication
  MLX90614
  Connections with Raspberry Pi
  VCC - VCC (Pin 2)
  GND - GND (Pin 6)
  SDA - SDA (Pin 3)
  SCL - SCL (Pin5)
  Red - 5V
  Black - Ground
  Yellow - SDA
  Blue - SCL
  Pi Camera

custom parts:
  Rasberry Pi NIOR Camera: Camera
