# Fritzing sketch Fritzing_thesis (saved by Fritzing 0.9.3b)
breadboards: 1

parts:
  Raspberry_Pi_4_B+ = Raspberry Pi B+
  MLX90614_Temp_Sensor = MLX90614 [package=to-39]
  Raspberry_Camera = Rasberry Pi NIOR Camera [chip_label=IC package="DIP (Dual Inline) [THT]"]  # not connected
  Flash_Led = smd LED [color="Red (633nm)" package="1206 [SMD]"]

nets:
  N1: Raspberry_Pi_4_B+.GPIO2, MLX90614_Temp_Sensor.PWM_SDA
  N2: Raspberry_Pi_4_B+.GPIO3, MLX90614_Temp_Sensor.SCL_VZ
  GND: Raspberry_Pi_4_B+.GND, MLX90614_Temp_Sensor.VSS, Flash_Led.cathode
  5V: Raspberry_Pi_4_B+.5V, MLX90614_Temp_Sensor.VDD, Flash_Led.anode

notes:
  Non Contact Temperature
  Sensor - i2c Communication
  MLX90614
  Connections with Raspberry Pi
  VCC - VCC (Pin 2)
  GND - GND (Pin 6)
  SDA - SDA (Pin 3)
  SCL - SCL (Pin5)
  Red - 5V
  Black - Ground
  Yellow - SDA
  Blue - SCL
  Pi Camera

custom parts:
  Rasberry Pi NIOR Camera: Camera
